// Logisim project ALU8.circ as structural Verilog: 11 circuits, main circuit main
module main (
  input  [7:0] A,
  input  [7:0] B,
  input  Cin,
  input  [3:0] OP,
  output Cout,
  output ZF,
  output SF,
  output OF,
  output [7:0] F
);

  // ALU alu_1: pin names not known; wires that end beside it: A, B, Cin, Cout, ZF, OP, SF, OF, F
endmodule

module ALU (
  input  [7:0] A,
  input  [7:0] B,
  input  Cin,
  input  [3:0] OP,
  output ZF,
  output SF,
  output [7:0] F,
  output OF,
  output Cout
);

  wire addl_1_cout, addl_1_of, andl_1_of, asrl_1_cout, asrl_1_of, iszero_1_out_2, lsll_1_cout, lsll_1_of,
       subl_1_cout, subl_1_of, xorl_1_of;
  wire [7:0] addl_1_f, andl_1_f, asrl_1_f, lsll_1_f, subl_1_f, xorl_1_f;

  addl addl_1 (.Cin(Cin), .A(A), .F(addl_1_f), .B(B), .Cout(addl_1_cout), .OF(addl_1_of));
  subl subl_1 (.Cin(Cin), .A(A), .F(subl_1_f), .B(B), .Cout(subl_1_cout), .OF(subl_1_of));
  andl andl_1 (.A(A), .B(B), .F(andl_1_f), .OF(andl_1_of));
  xorl xorl_1 (.A(A), .B(B), .F(xorl_1_f), .OF(xorl_1_of));
  asrl asrl_1 (.A(A), .F(asrl_1_f), .Cout(asrl_1_cout), .OF(asrl_1_of));
  lsll lsll_1 (.A(A), .F(lsll_1_f), .OF(lsll_1_of), .Cout(lsll_1_cout));
  Multiplexer #(.select(4), .enable("false")) multiplexer_1 (
    .in0(addl_1_of), .in1(subl_1_of), .in2(andl_1_of), .in3(xorl_1_of), .in4(asrl_1_of), .in5(lsll_1_of),
    .out(OF), .sel(OP));  // open: in6, in7, in8, in9, in10, in11, in12, in13, in14, in15
  Multiplexer #(.select(4), .enable("false")) multiplexer_2 (
    .in0(addl_1_cout), .in1(subl_1_cout), .in4(asrl_1_cout), .in5(lsll_1_cout), .out(Cout), .sel(OP));  // open: in2, in3, in6, in7, in8, in9, in10, in11, in12, in13, in14, in15
  Multiplexer #(.select(4), .width(8), .disabled(0), .enable("false")) multiplexer_3 (
    .in0(addl_1_f), .in1(subl_1_f), .in2(andl_1_f), .in3(xorl_1_f), .in4(asrl_1_f), .in5(lsll_1_f), .out(F),
    .sel(OP));  // open: in6, in7, in8, in9, in10, in11, in12, in13, in14, in15
  not not_1 (ZF, iszero_1_out_2);
  isZero iszero_1 (.in_1(F), .out_2(iszero_1_out_2));

  assign SF = F[7];
endmodule

module addl (
  input  Cin,
  input  [7:0] A,
  input  [7:0] B,
  output [7:0] F,
  output Cout,
  output OF
);

  wire and_1_out, and_2_out, fullbitadder_1_cout, fullbitadder_2_cout, fullbitadder_3_cout,
       fullbitadder_4_cout, fullbitadder_5_cout, fullbitadder_6_cout, fullbitadder_8_cout, not_1_out,
       not_2_out, not_3_out;

  fullBitAdder fullbitadder_1 (.A(A[0]), .B(B[0]), .Cin(Cin), .sum(F[0]), .Cout(fullbitadder_1_cout));
  fullBitAdder fullbitadder_2 (.A(A[1]), .B(B[1]), .Cin(fullbitadder_1_cout), .sum(F[1]), .Cout(fullbitadder_2_cout));
  fullBitAdder fullbitadder_3 (.A(A[2]), .B(B[2]), .Cin(fullbitadder_2_cout), .sum(F[2]), .Cout(fullbitadder_3_cout));
  fullBitAdder fullbitadder_4 (.A(A[4]), .B(B[4]), .Cin(fullbitadder_5_cout), .sum(F[4]), .Cout(fullbitadder_4_cout));
  fullBitAdder fullbitadder_5 (.A(A[3]), .B(B[3]), .Cin(fullbitadder_3_cout), .sum(F[3]), .Cout(fullbitadder_5_cout));
  fullBitAdder fullbitadder_6 (.A(A[5]), .B(B[5]), .Cin(fullbitadder_4_cout), .sum(F[5]), .Cout(fullbitadder_6_cout));
  fullBitAdder fullbitadder_7 (.A(A[7]), .B(B[7]), .Cin(fullbitadder_8_cout), .sum(F[7]), .Cout(Cout));
  fullBitAdder fullbitadder_8 (.A(A[6]), .B(B[6]), .Cin(fullbitadder_6_cout), .sum(F[6]), .Cout(fullbitadder_8_cout));
  not not_1 (not_1_out, B[7]);
  not not_2 (not_2_out, A[7]);
  not not_3 (not_3_out, F[7]);
  and and_1 (and_1_out, A[7], not_3_out, B[7]);
  and and_2 (and_2_out, not_1_out, F[7], not_2_out);
  or or_1 (OF, and_1_out, and_2_out);
endmodule

module subl (
  input  Cin,
  input  [7:0] A,
  input  [7:0] B,
  output [7:0] F,
  output Cout,
  output OF
);

  wire and_1_out, and_2_out, fullbitsubtracter_1_cout, fullbitsubtracter_2_cout, fullbitsubtracter_3_cout,
       fullbitsubtracter_4_cout, fullbitsubtracter_5_cout, fullbitsubtracter_6_cout,
       fullbitsubtracter_7_cout, not_1_out, not_2_out, not_3_out;

  fullBitSubtracter fullbitsubtracter_1 (
    .A(A[1]), .B(B[1]), .Cin(fullbitsubtracter_2_cout), .sum(F[1]), .Cout(fullbitsubtracter_1_cout));
  fullBitSubtracter fullbitsubtracter_2 (.A(A[0]), .B(B[0]), .Cin(Cin), .sum(F[0]), .Cout(fullbitsubtracter_2_cout));
  fullBitSubtracter fullbitsubtracter_3 (
    .A(A[2]), .B(B[2]), .Cin(fullbitsubtracter_1_cout), .sum(F[2]), .Cout(fullbitsubtracter_3_cout));
  fullBitSubtracter fullbitsubtracter_4 (
    .A(A[4]), .B(B[4]), .Cin(fullbitsubtracter_5_cout), .sum(F[4]), .Cout(fullbitsubtracter_4_cout));
  fullBitSubtracter fullbitsubtracter_5 (
    .A(A[3]), .B(B[3]), .Cin(fullbitsubtracter_3_cout), .sum(F[3]), .Cout(fullbitsubtracter_5_cout));
  fullBitSubtracter fullbitsubtracter_6 (
    .A(A[5]), .B(B[5]), .Cin(fullbitsubtracter_4_cout), .sum(F[5]), .Cout(fullbitsubtracter_6_cout));
  fullBitSubtracter fullbitsubtracter_7 (
    .A(A[6]), .B(B[6]), .Cin(fullbitsubtracter_6_cout), .sum(F[6]), .Cout(fullbitsubtracter_7_cout));
  fullBitSubtracter fullbitsubtracter_8 (.A(A[7]), .B(B[7]), .Cin(fullbitsubtracter_7_cout), .sum(F[7]), .Cout(Cout));
  and and_1 (and_1_out, A[7], not_1_out, not_2_out);
  not not_1 (not_1_out, F[7]);
  not not_2 (not_2_out, B[7]);
  not not_3 (not_3_out, A[7]);
  and and_2 (and_2_out, not_3_out, F[7], B[7]);
  or or_1 (OF, and_1_out, and_2_out);
endmodule

module andl (
  input  [7:0] A,
  input  [7:0] B,
  output OF,
  output [7:0] F
);

  assign F = A & B;  // AND_Gate and_1, 8 bits wide

  assign OF = 1'b0;
endmodule

module xorl (
  input  [7:0] A,
  input  [7:0] B,
  output OF,
  output [7:0] F
);

  assign F = A | B;  // OR_Gate or_1, 8 bits wide

  assign OF = 1'b0;
endmodule

module asrl (
  input  [7:0] A,
  output OF,
  output Cout,
  output [7:0] F
);


  assign Cout = A[0];
  assign F = {{2{A[7]}}, A[6:1]};
  assign OF = 1'b0;
endmodule

module lsll (
  input  [7:0] A,
  output OF,
  output [7:0] F,
  output Cout
);


  assign Cout = A[7];
  assign F = {A[6:0], 1'b0};
  assign OF = 1'b0;
endmodule

module fullBitAdder (
  input  A,
  input  B,
  input  Cin,
  output sum,
  output Cout
);

  wire and_1_out, and_2_out, xor_1_out, xor_2_out;

  xor xor_1 (xor_1_out, A, B);
  and and_1 (and_1_out, A, B);
  and and_2 (and_2_out, Cin, xor_2_out);
  xor xor_2 (xor_2_out, A, B);
  xor xor_3 (sum, xor_1_out, Cin);
  or or_1 (Cout, and_1_out, and_2_out);
endmodule

module fullBitSubtracter (
  input  A,
  input  B,
  input  Cin,
  output sum,
  output Cout
);

  wire and_1_out, and_2_out, and_3_out, not_1_out, not_2_out, or_1_out, xor_1_out;

  not not_1 (not_1_out, A);
  not not_2 (not_2_out, A);
  xor xor_1 (xor_1_out, A, B);
  and and_1 (and_1_out, not_1_out, Cin);
  and and_2 (and_2_out, not_2_out, B);
  xor xor_2 (sum, xor_1_out, Cin);
  or or_1 (or_1_out, and_1_out, and_2_out);
  and and_3 (and_3_out, B, Cin);
  or or_2 (Cout, or_1_out, and_3_out);
endmodule

module isZero (
  input  [7:0] in_1,
  output out_2
);

  or or_1 (out_2, in_1[0], in_1[1], in_1[2], in_1[3], in_1[4], in_1[5], in_1[6], in_1[7]);
endmodule
